// Logisim project lab10part2-bjc76.circ as structural Verilog: 1 circuit, main circuit main
module main (
  output [3:0] out_1
);

  wire clock_1_out, counter_2_carry, counter_3_carry, nand_1_out, Reset_out;
  wire [3:0] counter_1_q, counter_3_q;

  Clock clock_1 (.out(clock_1_out));
  Button Reset (.out(Reset_out));
  Counter #(.width(4), .max('hf), .ongoal("stay")) counter_1 (
    .Q(counter_1_q), .clk(clock_1_out), .clr(Reset_out));  // open: load, D, count, carry
  RAM #(.addrWidth(4), .dataWidth(4)) ram_1 (
    .addr(counter_1_q), .data(out_1), .sel(nand_1_out), .clk(clock_1_out), .ld(1'b0), .clr(Reset_out));
  assign out_1 = nand_1_out ? counter_3_q : 4'bz;  // Controlled_Buffer controlled_buffer_1
  Counter #(.width(5), .max('h10), .ongoal("stay")) counter_2 (
    .carry(counter_2_carry), .clk(clock_1_out), .clr(Reset_out));  // open: load, D, count, Q
  Counter #(.width(4), .max('hf), .ongoal("stay")) counter_3 (
    .Q(counter_3_q), .carry(counter_3_carry), .clk(clock_1_out), .clr(Reset_out));  // open: load, D, count
  nand nand_1 (nand_1_out, counter_3_carry, counter_2_carry);
endmodule
