// Logisim project lab11partC-bjc76.circ as structural Verilog: 2 circuits, main circuit main
module main (
);

  wire and_1_out, button_1_out, clock_1_out;
  wire [1:0] next_state_1_newstate, register_1_q;

  Button button_1 (.out(button_1_out));
  Register #(.width(2)) register_1 (.D(next_state_1_newstate), .Q(register_1_q), .clk(clock_1_out));  // open: en, clr
  Clock clock_1 (.out(clock_1_out));
  Next_State next_state_1 (.State(register_1_q), .Input(button_1_out), .NewState(next_state_1_newstate));
  and and_1 (and_1_out, register_1_q[0], register_1_q[1]);
  LED led_1 (.in(and_1_out));
endmodule

module Next_State (
  input  [1:0] State,
  input  Input,
  output [1:0] NewState
);

  wire and_1_out, and_2_out, and_3_out, and_4_out, and_5_out, not_1_out, not_2_out, not_3_out, not_4_out,
       not_5_out, not_6_out;

  not not_1 (not_1_out, State[1]);
  not not_2 (not_2_out, State[0]);
  not not_3 (not_3_out, State[1]);
  not not_4 (not_4_out, State[0]);
  not not_5 (not_5_out, State[0]);
  not not_6 (not_6_out, Input);
  and and_1 (and_1_out, not_1_out, State[0], Input);
  and and_2 (and_2_out, State[1], not_2_out);
  and and_3 (and_3_out, not_3_out, not_4_out, Input);
  and and_4 (and_4_out, State[1], not_5_out, not_6_out);
  and and_5 (and_5_out, State[1], State[0], Input);
  or or_1 (NewState[1], and_1_out, and_2_out);
  or or_2 (NewState[0], and_3_out, and_4_out, and_5_out);
endmodule
