// Logisim project Lab12-bjc76.circ as structural Verilog: 5 circuits, main circuit main
module main (
);

  wire Clock_out, decoder_1_mux, Reset_out, split_1_register;
  wire [1:0] decoder_1_aluop;
  wire [3:0] split_1_opcode;
  wire [7:0] adder_1_out, alu_1_out, bit_extender_1_out, multiplexer_1_out, register_1_q, register_2_a,
       register_2_b, split_1_immediate;
  wire [15:0] rom_1_data;

  assign bit_extender_1_out = {{7{1'b0}}, 1'b1};  // Bit_Extender bit_extender_1
  Register_part register_1 (.D(adder_1_out), .en(1'b1), .Q(register_1_q), .clk(Clock_out), .clr(Reset_out));
  Button Reset (.out(Reset_out));
  Clock Clock (.out(Clock_out));
  Adder adder_1 (.a(bit_extender_1_out), .b(register_1_q), .out(adder_1_out), .cin(1'b0));  // open: cout
  Split split_1 (
    .in_1(rom_1_data), .Immediate(split_1_immediate), .Register(split_1_register), .Opcode(split_1_opcode));
  ROM #(.dataWidth(16)) rom_1 (.addr(register_1_q), .data(rom_1_data), .sel(1'b1));
  Decoder decoder_1 (.Opcode(split_1_opcode), .ALUOP(decoder_1_aluop), .MUX(decoder_1_mux));
  Multiplexer #(.width(8), .enable("false")) multiplexer_1 (
    .in0(alu_1_out), .in1(split_1_immediate), .out(multiplexer_1_out), .sel(decoder_1_mux));
  Register register_2 (
    .Write_Data(multiplexer_1_out), .Write_Register(split_1_register), .Clock(Clock_out), .Reset(Reset_out),
    .A(register_2_a), .B(register_2_b));
  ALU alu_1 (.A(register_2_a), .B(register_2_b), .Opcode(decoder_1_aluop), .Out(alu_1_out));
endmodule

module Split (
  input  [15:0] in_1,
  output [7:0] Immediate,
  output Register,
  output [3:0] Opcode
);


  assign Immediate = in_1[7:0];
  assign Opcode = in_1[15:12];
  assign Register = in_1[11];
endmodule

// Reg
module Register (
  input  [7:0] Write_Data,
  input  Write_Register,
  input  Clock,
  input  Reset,
  output [7:0] A,
  output [7:0] B
);

  wire demultiplexer_1_out0, demultiplexer_1_out1;

  Demultiplexer #(.enable("false")) demultiplexer_1 (
    .out0(demultiplexer_1_out0), .out1(demultiplexer_1_out1), .in(1'b1), .sel(Write_Register));
  Register_part register_1 (.D(Write_Data), .en(demultiplexer_1_out0), .Q(A), .clk(Clock), .clr(Reset));
  Register_part register_2 (.D(Write_Data), .en(demultiplexer_1_out1), .Q(B), .clk(Clock), .clr(Reset));
endmodule

module ALU (
  input  [1:0] Opcode,
  input  [7:0] A,
  input  [7:0] B,
  output [7:0] Out
);

  wire [7:0] adder_1_out, nand_1_out, nor_1_out, subtractor_1_out;

  Adder adder_1 (.a(A), .b(B), .out(adder_1_out));  // open: cin, cout
  Subtractor subtractor_1 (.a(A), .b(B), .out(subtractor_1_out));  // open: bin, bout
  assign nor_1_out = ~(A | B);  // NOR_Gate nor_1, 8 bits wide
  assign nand_1_out = ~(A & B);  // NAND_Gate nand_1, 8 bits wide
  Multiplexer #(.select(2), .width(8), .enable("false")) multiplexer_1 (
    .in0(adder_1_out), .in1(subtractor_1_out), .in2(nor_1_out), .in3(nand_1_out), .out(Out), .sel(Opcode));
endmodule

// Decode
module Decoder (
  input  [3:0] Opcode,
  output [1:0] ALUOP,
  output MUX
);

  wire not_2_out, not_3_out;

  not not_1 (ALUOP[1], Opcode[2]);
  not not_2 (not_2_out, Opcode[3]);
  and and_1 (MUX, not_2_out, not_3_out);
  not not_3 (not_3_out, Opcode[2]);

  assign ALUOP[0] = Opcode[0];
endmodule
